# Fritzing sketch CircuitHandandMech (saved by Fritzing 0.9.4)

parts:
  Part1 = Arduino Uno (Rev3) - ICSP
  Servo_5 = Basic Servo
  M1 = Stepper Motor - Bipolar
  R1 = Basic Flex Resistor
  R2 = Basic Flex Resistor
  Servo_2 = Basic Servo
  Servo_4 = Basic Servo
  Servo_3 = Basic Servo
  Servo_6 = Basic Servo
  R3 = Resistor [tolerance=±5% resistance=10k package="2010 [SMD]"]
  R4 = Resistor [tolerance=±5% resistance=10k package="2010 [SMD]"]
  C3 = Capacitor Polarized [package=panasonic_d]
  Part3 = Thumb Joystick
  U1 = Transformer [package=transformer]
  D2 = Rectifier Diode [part_number=1N4001 package="Melf DO-213 AB [SMD]"]
  D3 = Rectifier Diode [part_number=1N4001 package="Melf DO-213 AB [SMD]"]
  D4 = Rectifier Diode [part_number=1N4001 package="Melf DO-213 AB [SMD]"]
  D5 = Rectifier Diode [part_number=1N4001 package="Melf DO-213 AB [SMD]"]
  U2 = Voltage Regulator - 5V [package="TO220 [THT]"]
  C4 = Capacitor Polarized [package=cpol-radial-1000uf-25v]
  X1 = X113647 Stepper Driver Board [package=board]

nets:
  N1: Part1.A2, Part3.VERT
  N2: Part1.A3, Part3.HORZ
  N3: Part1.A4/SDA, R2.Pin_2
  N4: Part1.A5/SCL, R1.pin_1
  N5: Part1.D9_PWM, X1.IN4
  N6: Part1.D10_PWM/SS, X1.IN3
  N7: Part1.D11_PWM/MOSI, X1.IN2
  N8: Part1.D12/MISO, X1.IN1
  GND: Part1.GND, Servo_5.gnd, Servo_2.gnd, Servo_4.gnd, Servo_3.gnd, Servo_6.gnd, R3.Pin_1, R4.Pin_1, C3.-, Part3.GND, D3.anode, D5.anode, U2.GND, X1.GND
  N9: Part1.D2, Servo_2.pulse
  N10: Part1.D3_PWM, Servo_6.pulse
  N11: Part1.D4, Servo_5.pulse
  N12: Part1.D5_PWM, Servo_4.pulse
  N13: Part1.D6_PWM, Servo_3.pulse
  N14: Part1.D7, Part3.SEL
  5V: Part1.5V, R1.Pin_2, R2.pin_1, Part3.VCC
  VCC: Part1.VIN, Servo_5.vcc, Servo_2.vcc, Servo_4.vcc, Servo_3.vcc, Servo_6.vcc, C3.+, U2.output_voltage, X1.+V
  N15: M1.A, X1.BLUE
  N16: M1.C, X1.PINK
  N17: M1.B, X1.YELLOW
  N18: M1.D, X1.ORANGE
  N19: U1.3, D3.cathode, D4.anode
  N20: U1.4, D2.anode, D5.cathode
  N21: D2.cathode, D4.cathode, U2.input_voltage, C4.+

notes:
  220V AC
  12V

custom parts:
  X113647 Stepper Driver Board: A common stepper motor driver board based on ULN2003APG darlington array
